# Fritzing sketch ear_say_animatronic_robot_horse_ears (saved by Fritzing 0.9.3b)

parts:
  Part1 = Adafruit Circuit Playground Dev Edition [part_number="Adafruit #3000"]
  J1 = Basic Servo
  J2 = Basic Servo
  BATT1 = 4xAA Switchable Battery Pack w/JST connector  # not connected

nets:
  GND: Part1.GND, J1.gnd, J2.gnd
  N1: Part1.D9, J1.pulse
  N2: Part1.D10, J2.pulse
  VCC: Part1.VBAT, J1.vcc, J2.vcc

notes:
  Left ear
  Right ear

custom parts:
  Adafruit Circuit Playground Dev Edition: Would you like to learn electronics, with an all-in-one board that has sensors and LEDs built in? Circuit Playground is here - and it's the best way to practice programming on real hardware with no soldering or sewing required! Circuit Playground features an ATmega32u4 processor, just like our popular Flora. The board's also round and has alligator-clip pads around it so you don't have to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
  4xAA Switchable Battery Pack w/JST connector: 4xAA Switchable Battery Pack with JST connector
